// Logisim project Adder and Subtractor.circ as structural Verilog: 1 circuit, main circuit main
module main (
  input  in_1,
  input  [3:0] A_INPUT,
  input  [3:0] B_INPUT,
  output [3:0] out_4,
  output c4
);

  wire adder_1_cout, adder_2_cout, adder_3_cout, xor_1_out, xor_2_out, xor_3_out, xor_4_out;

  xor xor_1 (xor_1_out, in_1, B_INPUT[0]);
  xor xor_2 (xor_2_out, in_1, B_INPUT[1]);
  xor xor_3 (xor_3_out, in_1, B_INPUT[2]);
  xor xor_4 (xor_4_out, in_1, B_INPUT[3]);
  Adder #(.width(1)) adder_1 (.a(A_INPUT[0]), .b(xor_1_out), .out(out_4[0]), .cin(in_1), .cout(adder_1_cout));
  Adder #(.width(1)) adder_2 (.a(A_INPUT[1]), .b(xor_2_out), .out(out_4[1]), .cin(adder_1_cout), .cout(adder_2_cout));
  Adder #(.width(1)) adder_3 (.a(A_INPUT[2]), .b(xor_3_out), .out(out_4[2]), .cin(adder_2_cout), .cout(adder_3_cout));
  Adder #(.width(1)) adder_4 (.a(A_INPUT[3]), .b(xor_4_out), .out(out_4[3]), .cin(adder_3_cout), .cout(c4));

  // Notes on the sheet:
  //   0 is add and then 1 is subtract.
endmodule
