// Logisim project ControlUnits.circ as structural Verilog
module main (
  input  A,
  input  B,
  input  C,
  input  D,
  output Y1,
  output Y2,
  output Y3,
  output Y4,
  output Y5,
  output Y6,
  output Y7,
  output Y8,
  output Y9,
  output Y10,
  output Y11
);

  wire and_1_out, and_2_out, and_3_out, and_4_out, and_5_out, and_6_out, and_7_out, and_8_out, and_9_out,
       and_10_out, and_11_out, and_12_out, and_14_out, and_15_out, and_16_out, and_18_out, and_19_out,
       not_1_out, not_2_out, not_3_out, not_4_out, not_5_out, not_6_out, not_7_out, not_8_out, not_9_out,
       not_10_out, not_11_out, not_12_out, not_13_out, not_14_out, not_15_out, not_16_out, not_17_out,
       not_18_out, not_19_out, not_20_out, not_21_out;

  and and_1 (and_1_out, A, C, not_1_out);
  not not_1 (not_1_out, D);
  not not_2 (not_2_out, A);
  and and_2 (and_2_out, not_2_out, C);
  not not_3 (not_3_out, B);
  and and_3 (and_3_out, not_3_out, C, not_4_out);
  not not_4 (not_4_out, D);
  not not_5 (not_5_out, A);
  and and_4 (and_4_out, not_5_out, D);
  not not_6 (not_6_out, B);
  and and_5 (and_5_out, A, not_6_out, not_7_out);
  not not_7 (not_7_out, C);
  and and_6 (and_6_out, A, C, not_8_out);
  not not_8 (not_8_out, D);
  not not_9 (not_9_out, C);
  not not_10 (not_10_out, A);
  and and_7 (and_7_out, C, D);
  and and_8 (and_8_out, B, not_11_out);
  not not_11 (not_11_out, D);
  not not_12 (not_12_out, B);
  and and_9 (and_9_out, A, not_12_out, not_13_out);
  not not_13 (not_13_out, D);
  and and_10 (and_10_out, A, not_14_out);
  not not_14 (not_14_out, C);
  and and_11 (and_11_out, B, D);
  and and_12 (and_12_out, A, C);
  and and_13 (Y8, A, not_15_out);
  not not_15 (not_15_out, C);
  not not_16 (not_16_out, A);
  and and_14 (and_14_out, not_16_out, not_17_out);
  not not_17 (not_17_out, D);
  not not_18 (not_18_out, B);
  and and_15 (and_15_out, not_18_out, not_19_out);
  not not_19 (not_19_out, D);
  not not_20 (not_20_out, C);
  and and_16 (and_16_out, not_20_out, not_21_out);
  not not_21 (not_21_out, D);
  and and_17 (Y10, A, C);
  and and_18 (and_18_out, A, C, D);
  and and_19 (and_19_out, A, B, C);
  or or_1 (Y1, B, and_1_out);
  or or_2 (Y2, and_2_out, and_3_out);
  or or_3 (Y3, and_4_out, and_5_out, and_6_out);
  and and_20 (Y4, A, B, not_9_out, D);
  or or_4 (Y5, not_10_out, and_7_out, and_8_out);
  or or_5 (Y6, and_9_out, and_10_out);
  or or_6 (Y7, and_11_out, and_12_out);
  or or_7 (Y9, and_14_out, and_15_out, and_16_out);
  or or_8 (Y11, and_18_out, and_19_out);
endmodule

module ALU (
  input  A_L,
  input  [1:0] SpecificOp,
  input  [15:0] in_3,
  input  [15:0] in_4,
  output FLAG,
  output [15:0] OUTPUT
);

  wire adder_1_cout, and_2_out, subtractor_1_bout;
  wire [15:0] adder_1_out, and_1_out, divider_1_out, divider_1_rem, multiplexer_1_out, multiplexer_2_out,
       multiplier_1_cout, multiplier_1_out, negator_1_out, or_1_out, subtractor_1_out, xor_1_out;

  Adder #(.width(16)) adder_1 (.a(in_3), .b(in_4), .out(adder_1_out), .cout(adder_1_cout));  // open: cin
  Subtractor #(.width(16)) subtractor_1 (
    .a(in_3), .b(in_4), .out(subtractor_1_out), .bout(subtractor_1_bout));  // open: bin
  Multiplier #(.width(16)) multiplier_1 (
    .a(in_3), .b(in_4), .out(multiplier_1_out), .cout(multiplier_1_cout));  // open: cin
  Divider #(.width(16)) divider_1 (.a(in_3), .b(in_4), .out(divider_1_out), .rem(divider_1_rem));  // open: upper
  assign and_1_out = in_3 & in_4;  // AND_Gate and_1, 16 bits wide
  assign or_1_out = in_3 | in_4;  // OR_Gate or_1, 16 bits wide
  assign xor_1_out = in_3 ^ in_4;  // XOR_Gate xor_1, 16 bits wide
  Negator #(.width(16)) negator_1 (.in(in_3), .out(negator_1_out));
  Multiplexer #(.select(2), .width(16), .enable("false")) multiplexer_1 (
    .in0(adder_1_out), .in1(subtractor_1_out), .in2(multiplier_1_out), .in3(divider_1_out),
    .out(multiplexer_1_out), .sel(SpecificOp));
  Multiplexer #(.select(2), .width(16), .enable("false")) multiplexer_2 (
    .in0(and_1_out), .in1(or_1_out), .in2(xor_1_out), .in3(negator_1_out), .out(multiplexer_2_out),
    .sel(SpecificOp));
  Multiplexer #(.width(16), .enable("false")) multiplexer_3 (
    .in0(multiplexer_1_out), .in1(multiplexer_2_out), .out(OUTPUT), .sel(A_L));
  and and_2 (and_2_out, multiplier_1_cout[0], multiplier_1_cout[1], multiplier_1_cout[2], multiplier_1_cout[3], multiplier_1_cout[4], multiplier_1_cout[5], multiplier_1_cout[6], multiplier_1_cout[7], multiplier_1_cout[8], multiplier_1_cout[9], multiplier_1_cout[10], multiplier_1_cout[11], multiplier_1_cout[12], multiplier_1_cout[13], multiplier_1_cout[14], multiplier_1_cout[15], divider_1_rem[0], divider_1_rem[1], divider_1_rem[2], divider_1_rem[3], divider_1_rem[4], divider_1_rem[5], divider_1_rem[6], divider_1_rem[7], divider_1_rem[8], divider_1_rem[9], divider_1_rem[10], divider_1_rem[11], divider_1_rem[12], divider_1_rem[13], divider_1_rem[14], divider_1_rem[15]);
  nor nor_1 (FLAG, adder_1_cout, subtractor_1_bout, and_2_out);

  // Notes on the sheet:
  //   A
  //   TR
  //   ADDER
  //   DIVIDER
  //   AND
  //   OR
  //   XOR
  //   SUBTRACTOR 
  //   MULTIPLIER
  //   NEGATION
endmodule

module RegisterFile (
  input  [3:0] WriteAddress,
  input  [15:0] WriteData,
  input  [3:0] ReadAddress_2,
  input  [3:0] ReadAddress_1,
  input  EnableWrite,
  input  Clock,
  input  ClearALL,
  output [15:0] ReadData_1,
  output [15:0] ReadData_2
);

  wire and_1_out, and_2_out, and_3_out, and_4_out, and_5_out, and_6_out, and_7_out, and_8_out, and_9_out,
       and_10_out, and_11_out, and_12_out, and_13_out, and_14_out, and_15_out, and_16_out, decoder_1_out0,
       decoder_1_out1, decoder_1_out2, decoder_1_out3, decoder_1_out4, decoder_1_out5, decoder_1_out6,
       decoder_1_out7, decoder_1_out8, decoder_1_out9, decoder_1_out10, decoder_1_out11, decoder_1_out12,
       decoder_1_out13, decoder_1_out14, decoder_1_out15;
  wire [15:0] register_1_q, register_2_q, register_3_q, register_4_q, register_5_q, register_6_q,
       register_7_q, register_8_q, register_9_q, register_10_q, register_11_q, register_12_q, register_13_q,
       register_14_q, register_15_q, register_16_q;

  Decoder #(.select(4)) decoder_1 (
    .out0(decoder_1_out0), .out1(decoder_1_out1), .out2(decoder_1_out2), .out3(decoder_1_out3),
    .out4(decoder_1_out4), .out5(decoder_1_out5), .out6(decoder_1_out6), .out7(decoder_1_out7),
    .out8(decoder_1_out8), .out9(decoder_1_out9), .out10(decoder_1_out10), .out11(decoder_1_out11),
    .out12(decoder_1_out12), .out13(decoder_1_out13), .out14(decoder_1_out14), .out15(decoder_1_out15),
    .sel(WriteAddress));  // open: en
  and and_1 (and_1_out, decoder_1_out0, EnableWrite);
  and and_2 (and_2_out, decoder_1_out1, EnableWrite);
  and and_3 (and_3_out, decoder_1_out2, EnableWrite);
  and and_4 (and_4_out, decoder_1_out3, EnableWrite);
  and and_5 (and_5_out, decoder_1_out4, EnableWrite);
  and and_6 (and_6_out, decoder_1_out5, EnableWrite);
  and and_7 (and_7_out, decoder_1_out6, EnableWrite);
  and and_8 (and_8_out, decoder_1_out7, EnableWrite);
  Register #(.width(16)) register_1 (.D(WriteData), .en(and_1_out), .Q(register_1_q), .clk(Clock), .clr(ClearALL));
  Register #(.width(16)) register_2 (.D(WriteData), .en(and_2_out), .Q(register_2_q), .clk(Clock), .clr(ClearALL));
  Register #(.width(16)) register_3 (.D(WriteData), .en(and_3_out), .Q(register_3_q), .clk(Clock), .clr(ClearALL));
  Register #(.width(16)) register_4 (.D(WriteData), .en(and_4_out), .Q(register_4_q), .clk(Clock), .clr(ClearALL));
  Register #(.width(16)) register_5 (.D(WriteData), .en(and_5_out), .Q(register_5_q), .clk(Clock), .clr(ClearALL));
  Register #(.width(16)) register_6 (.D(WriteData), .en(and_6_out), .Q(register_6_q), .clk(Clock), .clr(ClearALL));
  Register #(.width(16)) register_7 (.D(WriteData), .en(and_7_out), .Q(register_7_q), .clk(Clock), .clr(ClearALL));
  Register #(.width(16)) register_8 (.D(WriteData), .en(and_8_out), .Q(register_8_q), .clk(Clock), .clr(ClearALL));
  and and_9 (and_9_out, decoder_1_out8, EnableWrite);
  and and_10 (and_10_out, decoder_1_out9, EnableWrite);
  and and_11 (and_11_out, decoder_1_out10, EnableWrite);
  and and_12 (and_12_out, decoder_1_out11, EnableWrite);
  and and_13 (and_13_out, decoder_1_out12, EnableWrite);
  and and_14 (and_14_out, decoder_1_out13, EnableWrite);
  and and_15 (and_15_out, decoder_1_out14, EnableWrite);
  and and_16 (and_16_out, decoder_1_out15, EnableWrite);
  Register #(.width(16)) register_9 (.D(WriteData), .en(and_9_out), .Q(register_9_q), .clk(Clock), .clr(ClearALL));
  Register #(.width(16)) register_10 (.D(WriteData), .en(and_10_out), .Q(register_10_q), .clk(Clock), .clr(ClearALL));
  Register #(.width(16)) register_11 (.D(WriteData), .en(and_11_out), .Q(register_11_q), .clk(Clock), .clr(ClearALL));
  Register #(.width(16)) register_12 (.D(WriteData), .en(and_12_out), .Q(register_12_q), .clk(Clock), .clr(ClearALL));
  Register #(.width(16)) register_13 (.D(WriteData), .en(and_13_out), .Q(register_13_q), .clk(Clock), .clr(ClearALL));
  Register #(.width(16)) register_14 (.D(WriteData), .en(and_14_out), .Q(register_14_q), .clk(Clock), .clr(ClearALL));
  Register #(.width(16)) register_15 (.D(WriteData), .en(and_15_out), .Q(register_15_q), .clk(Clock), .clr(ClearALL));
  Register #(.width(16)) register_16 (.D(WriteData), .en(and_16_out), .Q(register_16_q), .clk(Clock), .clr(ClearALL));
  Multiplexer #(.select(4), .width(16)) multiplexer_1 (
    .in0(register_1_q), .in1(register_2_q), .in2(register_3_q), .in3(register_4_q), .in4(register_5_q),
    .in5(register_6_q), .in6(register_7_q), .in7(register_8_q), .in8(register_9_q), .in9(register_10_q),
    .in10(register_11_q), .in11(register_12_q), .in12(register_13_q), .in13(register_14_q),
    .in14(register_15_q), .in15(register_16_q), .out(ReadData_1), .sel(ReadAddress_1));  // open: en
  Multiplexer #(.select(4), .width(16)) multiplexer_2 (
    .in0(register_1_q), .in1(register_2_q), .in2(register_3_q), .in3(register_4_q), .in4(register_5_q),
    .in5(register_6_q), .in6(register_7_q), .in7(register_8_q), .in8(register_9_q), .in9(register_10_q),
    .in10(register_11_q), .in11(register_12_q), .in12(register_13_q), .in13(register_14_q),
    .in14(register_15_q), .in15(register_16_q), .out(ReadData_2), .sel(ReadAddress_2));  // open: en
endmodule
