// Logisim project TRUTH-TABLE.circ as structural Verilog: 1 circuit, main circuit main
module main (
  input  A,
  input  B,
  input  C,
  input  D,
  output [2:0] alu_sel,
  output Y4,
  output Y5,
  output Y6,
  output Y7
);

  wire not_1_out, not_2_out;

  or or_1 (alu_sel[2], B, A);
  or or_2 (alu_sel[0], D, A);
  and and_1 (Y4, A, D);
  not not_1 (not_1_out, A);
  not not_2 (not_2_out, D);
  or or_3 (Y5, not_1_out, not_2_out);

  assign alu_sel[1] = C;
  assign Y6 = A;
  assign Y7 = D;
endmodule
