// Logisim project multiplier.circ as structural Verilog: 1 circuit, main circuit main
module main (
  input  [7:0] A,
  input  [7:0] B,
  input  Cin,
  output [15:0] Output
);

  wire [6:0] and_54_out;
  wire [7:0] adder_1_cout, adder_2_cout, adder_3_cout, adder_4_cout, adder_5_cout, adder_6_cout, and_46_out,
       and_56_out, and_57_out, and_58_out, and_60_out, and_63_out, and_64_out;

  and and_1 (and_46_out[7], B[2], A[7]);
  and and_2 (and_54_out[6], B[0], A[7]);
  and and_3 (and_56_out[7], B[1], A[7]);
  and and_4 (and_56_out[6], B[1], A[6]);
  and and_5 (and_46_out[6], B[2], A[6]);
  and and_6 (and_57_out[7], B[3], A[7]);
  and and_7 (and_57_out[6], B[3], A[6]);
  and and_8 (and_58_out[7], B[4], A[7]);
  and and_9 (and_60_out[7], B[5], A[7]);
  and and_10 (and_63_out[7], B[6], A[7]);
  and and_11 (and_64_out[7], B[7], A[7]);
  and and_12 (and_54_out[5], B[0], A[6]);
  and and_13 (and_56_out[5], B[1], A[5]);
  and and_14 (and_46_out[4], B[2], A[4]);
  and and_15 (and_46_out[5], B[2], A[5]);
  and and_16 (and_57_out[5], B[3], A[5]);
  and and_17 (and_58_out[6], B[4], A[6]);
  and and_18 (and_60_out[5], B[5], A[5]);
  and and_19 (and_60_out[6], B[5], A[6]);
  and and_20 (and_63_out[6], B[6], A[6]);
  and and_21 (and_64_out[6], B[7], A[6]);
  and and_22 (and_54_out[3], B[0], A[4]);
  and and_23 (and_54_out[4], B[0], A[5]);
  and and_24 (and_56_out[4], B[1], A[4]);
  and and_25 (and_46_out[3], B[2], A[3]);
  Adder adder_1 (
    .a(and_46_out), .b(adder_2_cout), .out({adder_1_cout[6:0], Output[2]}), .cin(Cin), .cout(adder_1_cout[7]));
  and and_26 (and_57_out[4], B[3], A[4]);
  and and_27 (and_58_out[5], B[4], A[5]);
  and and_28 (and_58_out[4], B[4], A[4]);
  and and_29 (and_60_out[4], B[5], A[4]);
  and and_30 (and_63_out[5], B[6], A[5]);
  and and_31 (and_64_out[5], B[7], A[5]);
  and and_32 (and_54_out[2], B[0], A[3]);
  and and_33 (and_56_out[3], B[1], A[3]);
  and and_34 (and_56_out[2], B[1], A[2]);
  Adder adder_2 (
    .a(and_56_out), .b({Cin, and_54_out}), .out({adder_2_cout[6:0], Output[1]}), .cin(Cin),
    .cout(adder_2_cout[7]));
  and and_35 (and_46_out[2], B[2], A[2]);
  and and_36 (and_57_out[2], B[3], A[2]);
  and and_37 (and_57_out[3], B[3], A[3]);
  Adder adder_3 (
    .a(and_57_out), .b(adder_1_cout), .out({adder_3_cout[6:0], Output[3]}), .cin(Cin), .cout(adder_3_cout[7]));
  and and_38 (and_58_out[3], B[4], A[3]);
  Adder adder_4 (
    .a(and_58_out), .b(adder_3_cout), .out({adder_4_cout[6:0], Output[4]}), .cin(Cin), .cout(adder_4_cout[7]));
  and and_39 (and_60_out[3], B[5], A[3]);
  Adder adder_5 (
    .a(and_60_out), .b(adder_4_cout), .out({adder_5_cout[6:0], Output[5]}), .cin(Cin), .cout(adder_5_cout[7]));
  and and_40 (and_63_out[4], B[6], A[4]);
  and and_41 (and_63_out[3], B[6], A[3]);
  Adder adder_6 (
    .a(and_63_out), .b(adder_5_cout), .out({adder_6_cout[6:0], Output[6]}), .cin(Cin), .cout(adder_6_cout[7]));
  and and_42 (and_64_out[4], B[7], A[4]);
  and and_43 (and_64_out[3], B[7], A[3]);
  Adder adder_7 (.a(and_64_out), .b(adder_6_cout), .out(Output[14:7]), .cin(Cin), .cout(Output[15]));
  and and_44 (and_54_out[1], B[0], A[2]);
  and and_45 (and_56_out[1], B[1], A[1]);
  and and_46 (and_46_out[0], B[2], A[0]);
  and and_47 (and_46_out[1], B[2], A[1]);
  and and_48 (and_57_out[1], B[3], A[1]);
  and and_49 (and_58_out[2], B[4], A[2]);
  and and_50 (and_60_out[2], B[5], A[2]);
  and and_51 (and_60_out[1], B[5], A[1]);
  and and_52 (and_63_out[2], B[6], A[2]);
  and and_53 (and_64_out[2], B[7], A[2]);
  and and_54 (and_54_out[0], B[0], A[1]);
  and and_55 (Output[0], B[0], A[0]);
  and and_56 (and_56_out[0], B[1], A[0]);
  and and_57 (and_57_out[0], B[3], A[0]);
  and and_58 (and_58_out[0], B[4], A[0]);
  and and_59 (and_58_out[1], B[4], A[1]);
  and and_60 (and_60_out[0], B[5], A[0]);
  and and_61 (and_63_out[1], B[6], A[1]);
  and and_62 (and_64_out[1], B[7], A[1]);
  and and_63 (and_63_out[0], B[6], A[0]);
  and and_64 (and_64_out[0], B[7], A[0]);
endmodule
